# Fritzing sketch AnalogInputOutput (saved by Fritzing 0.1.b)
breadboards: 1

parts:
  Part1 = Arduino Diecimila (deprecated) [package=THT]
  LED1 = Red LED - 5mm
  R1 = Trimmer Potentiometer [package=THT]
  R2 = basic-resistor-220

nets:
  N1: Part1.D3, R2.connector1
  N2: Part1.+5V, R1.leg1
  N3: Part1.GND, Part1.ground, LED1.cathode, R1.leg2
  N4: Part1.A2, R1.wiper
  N5: LED1.anode, R2.connector0
