# Fritzing sketch Button (saved by Fritzing 0.1.b)
breadboards: 1

parts:
  Part1 = Arduino Diecimila (deprecated) [package=THT]
  S1 = Pushbutton [package=THT]
  R1 = basic-resistor-1k
  LED1 = Red LED - 5mm

nets:
  N1: Part1.GND, Part1.ground, R1.connector0, LED1.cathode
  N2: Part1.D13, LED1.anode
  N3: Part1.D2, S1.leg1, R1.connector1
  N4: Part1.+5V, S1.leg0
